// Logisim project b2_g1.circ as structural Verilog: 1 circuit, main circuit main
module main (
  input  [3:0] A,
  input  [3:0] B,
  input  [2:0] s2_s1_s0,
  output [3:0] X,
  output [3:0] Y,
  output [4:0] Z,
  output [3:0] F,
  output S,
  output C,
  output Z_2,
  output V
);

  wire n7404_1__2__1y, n7404_1__4__2y, n7404_1__6__3y, n7404_1__8__4y, n7404_1__10__5y, n7404_1__12__6y,
       n7408_1__3__1y, n7408_1__6__2y, n7408_2__3__1y, n7408_2__6__2y, n7408_2__8__3y, n7408_2__11__4y,
       n7432_3__6__2y, n7432_3__8__3y, n7432_3__11__4y, n7483_1__6__s2, n7483_1__14__cout, n7483_2__6__s2,
       n7483_2__14__cout, n7486_1__3__1y, n7486_1__6__2y, n7486_1__8__3y, n7486_1__11__4y;

  _7404 u_7404_1 (
    ._1__1A(s2_s1_s0[0]), ._2__1Y(n7404_1__2__1y), ._3__2A(s2_s1_s0[1]), ._4__2Y(n7404_1__4__2y),
    ._5__3A(B[3]), ._6__3Y(n7404_1__6__3y), ._7__GND(1'b0), ._14__Vcc(1'b1), ._13__6A(B[0]),
    ._12__6Y(n7404_1__12__6y), ._11__5A(B[1]), ._10__5Y(n7404_1__10__5y), ._9__4A(B[2]),
    ._8__4Y(n7404_1__8__4y));
  _7408 u_7408_1 (
    ._1__1A(s2_s1_s0[0]), ._2__1B(n7404_1__4__2y), ._3__1Y(n7408_1__3__1y), ._4__2A(n7404_1__2__1y),
    ._5__2B(s2_s1_s0[1]), ._6__2Y(n7408_1__6__2y), ._7__GND(1'b0), ._14__Vcc(1'b1), ._13__4B(n7483_2__6__s2),
    ._12__4A(n7404_1__4__2y), ._11__4Y(Z[1]), ._10__3B(s2_s1_s0[2]), ._9__3A(n7404_1__4__2y), ._8__3Y(Z[0]));
  _7432 u_7432_1 (
    ._1__1A(n7408_1__3__1y), ._2__1B(n7486_1__3__1y), ._3__1Y(Y[2]), ._4__2A(n7408_1__3__1y),
    ._5__2B(n7486_1__6__2y), ._6__2Y(Y[3]), ._7__GND(1'b0), ._14__Vcc(n7404_1__4__2y),
    ._13__4B(n7408_1__3__1y), ._12__4A(n7486_1__11__4y), ._11__4Y(Y[0]), ._10__3B(n7408_1__3__1y),
    ._9__3A(n7486_1__8__3y), ._8__3Y(Y[1]));
  _7432 u_7432_2 (
    ._1__1A(n7408_2__3__1y), ._2__1B(A[2]), ._3__1Y(X[2]), ._4__2A(n7408_2__6__2y), ._5__2B(A[3]),
    ._6__2Y(X[3]), ._7__GND(1'b0), ._14__Vcc(1'b1), ._13__4B(n7408_2__11__4y), ._12__4A(A[0]),
    ._11__4Y(X[0]), ._10__3B(n7408_2__8__3y), ._9__3A(A[1]), ._8__3Y(X[1]));
  _7408 u_7408_2 (
    ._1__1A(n7404_1__8__4y), ._2__1B(n7408_1__6__2y), ._3__1Y(n7408_2__3__1y), ._4__2A(n7404_1__6__3y),
    ._5__2B(n7408_1__6__2y), ._6__2Y(n7408_2__6__2y), ._7__GND(1'b0), ._14__Vcc(1'b1),
    ._13__4B(n7404_1__12__6y), ._12__4A(n7408_1__6__2y), ._11__4Y(n7408_2__11__4y),
    ._10__3B(n7404_1__10__5y), ._9__3A(n7408_1__6__2y), ._8__3Y(n7408_2__8__3y));
  _7486 u_7486_1 (
    ._1__1A(n7404_1__8__4y), ._2__1B(s2_s1_s0[0]), ._3__1Y(n7486_1__3__1y), ._4__2A(n7404_1__6__3y),
    ._5__2B(s2_s1_s0[0]), ._6__2Y(n7486_1__6__2y), ._7__GND(1'b0), ._14__Vcc(1'b1),
    ._13__4B(n7404_1__12__6y), ._12__4A(s2_s1_s0[0]), ._11__4Y(n7486_1__11__4y), ._10__3B(n7404_1__10__5y),
    ._9__3A(s2_s1_s0[0]), ._8__3Y(n7486_1__8__3y));
  _7408 u_7408_3 (
    ._4__2A(n7404_1__4__2y), ._5__2B(n7483_1__14__cout), ._6__2Y(C), ._7__GND(1'b0), ._14__Vcc(1'b1),
    ._13__4B(n7483_2__14__cout), ._12__4A(n7404_1__4__2y), ._11__4Y(Z[2]), ._10__3B(n7404_1__4__2y),
    ._9__3A(n7483_1__6__s2), ._8__3Y(Z[3]));  // open: _1__1A, _2__1B, _3__1Y
  _7483 u_7483_1 (
    ._1__A4(Y[3]), ._3__A3(1'b1), ._4__B3(Z[3]), ._5__Vcc(1'b1), ._6__S2(n7483_1__6__s2), ._7__B2(1'b0),
    ._8__A2(1'b0), ._16__B4(X[3]), ._15__S4(F[3]), ._14__Cout(n7483_1__14__cout), ._13__Cin(Z[2]),
    ._12__GND(1'b0), ._11__B1(Y[2]), ._10__A1(X[2]), ._9__S1(F[2]));  // open: _2__S3
  _7432 u_7432_3 (
    ._4__2A(F[3]), ._5__2B(n7432_3__8__3y), ._6__2Y(n7432_3__6__2y), ._7__GND(1'b0), ._14__Vcc(1'b1),
    ._13__4B(F[0]), ._12__4A(F[1]), ._11__4Y(n7432_3__11__4y), ._10__3B(n7432_3__11__4y), ._9__3A(F[2]),
    ._8__3Y(n7432_3__8__3y));  // open: _1__1A, _2__1B, _3__1Y
  _7483 u_7483_2 (
    ._1__A4(Y[1]), ._3__A3(1'b1), ._4__B3(Z[1]), ._5__Vcc(1'b1), ._6__S2(n7483_2__6__s2), ._7__B2(1'b0),
    ._8__A2(1'b0), ._16__B4(X[1]), ._15__S4(F[1]), ._14__Cout(n7483_2__14__cout), ._13__Cin(Z[0]),
    ._12__GND(1'b0), ._11__B1(Y[0]), ._10__A1(X[0]), ._9__S1(F[0]));  // open: _2__S3
  _7486 u_7486_2 (
    ._1__1A(n7432_3__6__2y), ._2__1B(1'b1), ._3__1Y(Z_2), ._4__2A(Z[3]), ._5__2B(C), ._6__2Y(V),
    ._7__GND(1'b0), ._14__Vcc(1'b1));  // open: _13__4B, _12__4A, _11__4Y, _10__3B, _9__3A, _8__3Y

  assign S = F[3];
  assign Z[4] = C;

  // Notes on the sheet:
  //   ~B3
  //   ~B2
  //   ~B0
  //   ~B1
endmodule
