// Logisim project ALU_16_bit.circ as structural Verilog: 1 circuit, main circuit ALU_16_bit
module ALU_16_bit (
  input  [15:0] ALU_A_IN,
  input  [15:0] ALU_B_IN,
  input  [2:0] OP_CODE,
  output [15:0] ALU_OUT,
  output Z,
  output N
);

  wire adder_1_cout;
  wire [15:0] adder_1_out, and_1_out, multiplexer_1_out, multiplexer_2_out, multiplexer_3_out,
       multiplexer_4_out, not_1_out, or_1_out, shifter_1_out, shifter_2_out, subtractor_1_out, xor_1_out;

  Adder #(.width(16)) adder_1 (.a(ALU_A_IN), .b(ALU_B_IN), .out(adder_1_out), .cout(adder_1_cout));  // open: cin
  Subtractor #(.width(16)) subtractor_1 (
    .a(ALU_A_IN), .b(ALU_B_IN), .out(subtractor_1_out), .bin(adder_1_cout));  // open: bout
  assign and_1_out = ALU_A_IN & ALU_B_IN;  // AND_Gate and_1, 16 bits wide
  assign or_1_out = ALU_A_IN | ALU_B_IN;  // OR_Gate or_1, 16 bits wide
  assign not_1_out = ~ALU_A_IN;  // NOT_Gate not_1, 16 bits wide
  assign xor_1_out = ALU_A_IN ^ ALU_B_IN;  // XOR_Gate xor_1, 16 bits wide
  Shifter #(.width(16), .shift("rl")) shifter_1 (.in(ALU_A_IN), .\dist (4'b0001), .out(shifter_1_out));
  Shifter #(.width(16), .shift("rr")) shifter_2 (.in(ALU_A_IN), .\dist (4'b0001), .out(shifter_2_out));
  Multiplexer #(.width(16), .enable("false")) multiplexer_1 (
    .in0(adder_1_out), .in1(subtractor_1_out), .out(multiplexer_1_out), .sel(OP_CODE[0]));
  Multiplexer #(.width(16), .enable("false")) multiplexer_2 (
    .in0(and_1_out), .in1(or_1_out), .out(multiplexer_2_out), .sel(OP_CODE[0]));
  Multiplexer #(.width(16), .enable("false")) multiplexer_3 (
    .in0(not_1_out), .in1(xor_1_out), .out(multiplexer_3_out), .sel(OP_CODE[0]));
  Multiplexer #(.width(16), .enable("false")) multiplexer_4 (
    .in0(shifter_1_out), .in1(shifter_2_out), .out(multiplexer_4_out), .sel(OP_CODE[0]));
  nor nor_1 (Z, ALU_OUT[0], ALU_OUT[1], ALU_OUT[2], ALU_OUT[3], ALU_OUT[4], ALU_OUT[5], ALU_OUT[6], ALU_OUT[7], ALU_OUT[8], ALU_OUT[9], ALU_OUT[10], ALU_OUT[11], ALU_OUT[12], ALU_OUT[13], ALU_OUT[14], ALU_OUT[15]);
  Multiplexer #(.select(2), .width(16), .enable("false")) multiplexer_5 (
    .in0(multiplexer_1_out), .in1(multiplexer_2_out), .in2(multiplexer_3_out), .in3(multiplexer_4_out),
    .out(ALU_OUT), .sel(OP_CODE[2:1]));

  assign N = ALU_OUT[15];
endmodule
