// Logisim project one-bit-ALU.circ as structural Verilog: 1 circuit, main circuit one-bit-ALU
module one_bit_ALU (
  input  [5:0] ALU_OpCode,
  input  Invert_B_Signal,
  input  A,
  input  B,
  input  C_In,
  input  less,
  output ALU_Result_1,
  output C_Out
);

  wire and_1_out, main_1_p5, multiplexer_1_out, not_1_out, or_1_out, xor_1_out;

  Multiplexer #(.disabled(0), .enable("false")) multiplexer_1 (
    .in0(B), .in1(not_1_out), .out(multiplexer_1_out), .sel(Invert_B_Signal));
  not not_1 (not_1_out, B);
  // one_bit_adder_main main_1: pin names not known; wires that end beside it: B, A, multiplexer_1_out, C_In, main_1_p5, C_Out
  and and_1 (and_1_out, A, multiplexer_1_out);
  or or_1 (or_1_out, A, multiplexer_1_out);
  xor xor_1 (xor_1_out, A, multiplexer_1_out);
  Multiplexer #(.select(3), .disabled(0), .enable("false")) multiplexer_2 (
    .in0(main_1_p5), .in1(main_1_p5), .in2(1'b0), .in3(and_1_out), .in4(or_1_out), .in5(xor_1_out),
    .in6(1'b0), .in7(less), .out(ALU_Result_1), .sel(ALU_OpCode[2:0]));
endmodule
