// Logisim project B2_Group1.circ as structural Verilog: 8 circuits, main circuit main
module main (
  input  [31:0] in_1,
  input  [31:0] in_2,
  output [31:0] Result,
  output Overflow,
  output Underflow
);

  FPA FPA (.X(in_1), .Y(in_2), .S(Result), .O(Overflow), .U(Underflow));

  // Notes on the sheet:
  //   100
  //   0.245
endmodule

module ExponentComparator (
  input  [9:0] X,
  input  [9:0] Y,
  output [9:0] larger,
  output x_y,
  output [4:0] difference
);

  wire ALU_2_n;
  wire [9:0] ALU_alu_out, MUX_2_out, negator_1_out;
  wire [9:5] MUX_3_out;
  wire [15:10] ALU_alu_out_2;

  ALU_16_bit ALU (
    .ALU_A_IN({{6{1'b0}}, X}), .ALU_B_IN({{6{1'b0}}, Y}), .OP_CODE(3'b001),
    .ALU_OUT({ALU_alu_out_2, ALU_alu_out}), .N(x_y));  // open: Z
  Negator #(.width(10)) negator_1 (.in(ALU_alu_out), .out(negator_1_out));
  MUX10bit MUX (._0(X), ._1(Y), .SELECT(x_y), .OUT(larger));
  MUX10bit MUX_2 (._0(ALU_alu_out), ._1(negator_1_out), .SELECT(x_y), .OUT(MUX_2_out));
  ALU_16_bit ALU_2 (
    .ALU_A_IN({{6{1'b0}}, MUX_2_out}), .ALU_B_IN(16'h1f), .OP_CODE(3'b001), .N(ALU_2_n));  // open: ALU_OUT, Z
  MUX10bit MUX_3 (._0(10'h1f), ._1(MUX_2_out), .SELECT(ALU_2_n), .OUT({MUX_3_out, difference}));
endmodule

module MUX10bit (
  input  [9:0] _0,
  input  [9:0] _1,
  input  SELECT,
  output [9:0] OUT
);

  _74157 u_74157_1 (
    ._1__S(SELECT), ._2__A1(_0[0]), ._3__B1(_1[0]), ._4__Y1(OUT[0]), ._5__A2(_0[1]), ._6__B2(_1[1]),
    ._7__Y2(OUT[1]), ._15__G(1'b0), ._14__A4(_0[2]), ._13__B4(_1[2]), ._12__Y4(OUT[2]), ._11__A3(_0[3]),
    ._10__B3(_1[3]), ._9__Y3(OUT[3]));  // open: _8__GND, _16__Vcc
  _74157 u_74157_2 (
    ._1__S(SELECT), ._2__A1(_0[4]), ._3__B1(_1[4]), ._4__Y1(OUT[4]), ._5__A2(_0[5]), ._6__B2(_1[5]),
    ._7__Y2(OUT[5]), ._15__G(1'b0), ._14__A4(_0[7]), ._13__B4(_1[7]), ._12__Y4(OUT[7]), ._11__A3(_0[6]),
    ._10__B3(_1[6]), ._9__Y3(OUT[6]));  // open: _8__GND, _16__Vcc
  _74157 u_74157_3 (
    ._1__S(SELECT), ._2__A1(_0[8]), ._3__B1(_1[8]), ._4__Y1(OUT[8]), ._5__A2(_0[9]), ._6__B2(_1[9]),
    ._7__Y2(OUT[9]), ._15__G(1'b0));  // open: _8__GND, _16__Vcc, _14__A4, _13__B4, _12__Y4, _11__A3, _10__B3, _9__Y3
endmodule

module FPA (
  input  [31:0] X,
  input  [31:0] Y,
  output [31:0] S,
  output O,
  output U
);

  wire comparator_1_eq, comparator_2_eq, Comparator_3_x_y, comparator_4_eq, Normalizer_2_overflow,
       Normalizer_overflow, Normalizer_underflow;
  wire [4:0] Comparator_3_difference;
  wire [9:0] Comparator_3_larger, Normalizer_2_expo_out, Normalizer_expo_out;
  wire [23:0] MUX_2_out_4, MUX_3_out_4, MUX_4_out_4, MUX_out_4, negator_1_out, negator_2_out;
  wire [31:0] ALU_2_c, ALU_c, mux32bit_1_out, MUX_5_out, MUX_6_out, negator_3_out, Normalizer_2_signi_out,
       Normalizer_signi_out, shifter_1_out, toBeAdded_to_round_tobeadded;

  Comparator #(.width(31)) comparator_1 (.a({31{1'b0}}), .b(X[30:0]), .eq(comparator_1_eq));  // open: gt, lt
  Comparator #(.width(31)) comparator_2 (.a({31{1'b0}}), .b(Y[30:0]), .eq(comparator_2_eq));  // open: gt, lt
  Negator #(.width(24)) negator_1 (.in({3'b001, X[20:0]}), .out(negator_1_out));
  Negator #(.width(24)) negator_2 (.in({3'b001, Y[20:0]}), .out(negator_2_out));
  MUX24bit MUX (.X({3'b001, X[20:0]}), .Y(negator_1_out), .S(X[31]), .out_4(MUX_out_4));
  MUX24bit MUX_2 (.X({3'b001, Y[20:0]}), .Y(negator_2_out), .S(Y[31]), .out_4(MUX_2_out_4));
  ExponentComparator Comparator_3 (
    .X(X[30:21]), .Y(Y[30:21]), .larger(Comparator_3_larger), .x_y(Comparator_3_x_y),
    .difference(Comparator_3_difference));
  MUX24bit MUX_3 (.X(MUX_2_out_4), .Y(MUX_out_4), .S(Comparator_3_x_y), .out_4(MUX_3_out_4));
  MUX24bit MUX_4 (.X(MUX_out_4), .Y(MUX_2_out_4), .S(Comparator_3_x_y), .out_4(MUX_4_out_4));
  ALU_32_bit ALU (
    .OpCode({6{1'b0}}), .Invert_B_Signal(1'b0), .A(Normalizer_2_signi_out), .B(toBeAdded_to_round_tobeadded),
    .Cin(1'b0), .C(ALU_c));  // open: Cout, OVF
  Normalizer Normalizer (
    .Significand(ALU_c), .Expo_in(Normalizer_2_expo_out), .signi_out(Normalizer_signi_out),
    .Expo_out(Normalizer_expo_out), .Overflow(Normalizer_overflow), .Underflow(Normalizer_underflow));
  Shifter #(.width(32), .shift("ar")) shifter_1 (
    .in({MUX_3_out_4, {8{1'b0}}}), .\dist (Comparator_3_difference), .out(shifter_1_out));
  ALU_32_bit ALU_2 (
    .OpCode({6{1'b0}}), .Invert_B_Signal(1'b0), .A({MUX_4_out_4, {8{1'b0}}}), .B(shifter_1_out), .Cin(1'b0),
    .C(ALU_2_c));  // open: Cout, OVF
  Negator #(.width(32)) negator_3 (.in(ALU_2_c), .out(negator_3_out));
  Comparator #(.width(32)) comparator_4 (.a(ALU_2_c), .b({32{1'b0}}), .eq(comparator_4_eq));  // open: gt, lt
  MUX32bit MUX_5 (._0(ALU_2_c), ._1(negator_3_out), .Select(ALU_2_c[31]), .out(MUX_5_out));
  MUX32bit MUX_6 (._0(mux32bit_1_out), ._1(Y), .Select(comparator_1_eq), .out(MUX_6_out));
  MUX32bit MUX_7 (._0(MUX_6_out), ._1(X), .Select(comparator_2_eq), .out(S));
  Normalizer Normalizer_2 (
    .Significand(MUX_5_out), .Expo_in(Comparator_3_larger), .signi_out(Normalizer_2_signi_out),
    .Expo_out(Normalizer_2_expo_out), .Overflow(Normalizer_2_overflow), .Underflow(U));
  _7432 u_7432_1 (
    ._1__1A(Normalizer_overflow), ._2__1B(Normalizer_2_overflow), ._3__1Y(O));  // open: _4__2A, _5__2B, _6__2Y, _7__GND, _14__Vcc, _13__4B, _12__4A, _11__4Y, _10__3B, _9__3A, _8__3Y
  Round_Up_or_Not toBeAdded_to_round (.Input(Normalizer_2_signi_out), .toBeAdded(toBeAdded_to_round_tobeadded));
  MUX32bit mux32bit_1 (
    ._0({ALU_2_c[31], Normalizer_expo_out, Normalizer_signi_out[28:8]}), ._1({32{1'b0}}),
    .Select(comparator_4_eq), .out(mux32bit_1_out));
endmodule

module MUX24bit (
  input  [23:0] X,
  input  [23:0] Y,
  input  S,
  output [23:0] out_4
);

  _74157 u_74157_1 (
    ._1__S(S), ._2__A1(X[0]), ._3__B1(Y[0]), ._4__Y1(out_4[0]), ._5__A2(X[1]), ._6__B2(Y[1]),
    ._7__Y2(out_4[1]), ._8__GND(1'b0), ._16__Vcc(1'b1), ._15__G(1'b0), ._14__A4(X[2]), ._13__B4(Y[2]),
    ._12__Y4(out_4[2]), ._11__A3(X[3]), ._10__B3(Y[3]), ._9__Y3(out_4[3]));
  _74157 u_74157_2 (
    ._1__S(S), ._2__A1(X[4]), ._3__B1(Y[4]), ._4__Y1(out_4[4]), ._5__A2(X[5]), ._6__B2(Y[5]),
    ._7__Y2(out_4[5]), ._8__GND(1'b0), ._16__Vcc(1'b1), ._15__G(1'b0), ._14__A4(X[7]), ._13__B4(Y[7]),
    ._12__Y4(out_4[7]), ._11__A3(X[6]), ._10__B3(Y[6]), ._9__Y3(out_4[6]));
  _74157 u_74157_3 (
    ._1__S(S), ._2__A1(X[8]), ._3__B1(Y[8]), ._4__Y1(out_4[8]), ._5__A2(X[9]), ._6__B2(Y[9]),
    ._7__Y2(out_4[9]), ._8__GND(1'b0), ._16__Vcc(1'b1), ._15__G(1'b0), ._14__A4(X[11]), ._13__B4(Y[11]),
    ._12__Y4(out_4[11]), ._11__A3(X[10]), ._10__B3(Y[10]), ._9__Y3(out_4[10]));
  _74157 u_74157_4 (
    ._1__S(S), ._2__A1(X[12]), ._3__B1(Y[12]), ._4__Y1(out_4[12]), ._5__A2(X[13]), ._6__B2(Y[13]),
    ._7__Y2(out_4[13]), ._8__GND(1'b0), ._16__Vcc(1'b1), ._15__G(1'b0), ._14__A4(X[15]), ._13__B4(Y[15]),
    ._12__Y4(out_4[15]), ._11__A3(X[14]), ._10__B3(Y[14]), ._9__Y3(out_4[14]));
  _74157 u_74157_5 (
    ._1__S(S), ._2__A1(X[16]), ._3__B1(Y[16]), ._4__Y1(out_4[16]), ._5__A2(X[17]), ._6__B2(Y[17]),
    ._7__Y2(out_4[17]), ._8__GND(1'b0), ._16__Vcc(1'b1), ._15__G(1'b0), ._14__A4(X[19]), ._13__B4(Y[19]),
    ._12__Y4(out_4[19]), ._11__A3(X[18]), ._10__B3(Y[18]), ._9__Y3(out_4[18]));
  _74157 u_74157_6 (
    ._1__S(S), ._2__A1(X[20]), ._3__B1(Y[20]), ._4__Y1(out_4[20]), ._5__A2(X[21]), ._6__B2(Y[21]),
    ._7__Y2(out_4[21]), ._8__GND(1'b0), ._16__Vcc(1'b1), ._15__G(1'b0), ._14__A4(X[23]), ._13__B4(Y[23]),
    ._12__Y4(out_4[23]), ._11__A3(X[22]), ._10__B3(Y[22]), ._9__Y3(out_4[22]));
endmodule

module Normalizer (
  input  [31:0] Significand,
  input  [9:0] Expo_in,
  output [31:0] signi_out,
  output [9:0] Expo_out,
  output Overflow,
  output Underflow
);

  wire ALU_2_z, ALU_n, comparator_1_eq, comparator_2_eq, n7432_1__3__1y, n7486_1__6__2y;
  wire [3:0] ALU_2_alu_out_2;
  wire [4:0] bitfinder_1_index;
  wire [15:0] ALU_3_alu_out, ALU_alu_out, negator_1_out;
  wire [15:10] ALU_2_alu_out;
  wire [31:0] shifter_1_out, shifter_2_out;

  Comparator #(.width(30)) comparator_1 (.a(Significand[29:0]), .b({30{1'b0}}), .eq(comparator_1_eq));  // open: gt, lt
  BitFinder #(.width(32), .\type ("high1")) bitfinder_1 (.in(Significand), .index(bitfinder_1_index));  // open: found
  Comparator #(.width(10)) comparator_2 (.a(Expo_in), .b({10{1'b0}}), .eq(comparator_2_eq));  // open: gt, lt
  ALU_16_bit ALU (
    .ALU_A_IN(16'h1d), .ALU_B_IN({{11{1'b0}}, bitfinder_1_index}), .OP_CODE(3'b001), .ALU_OUT(ALU_alu_out),
    .N(ALU_n));  // open: Z
  Shifter #(.width(32), .shift("lr")) shifter_1 (.in(Significand), .\dist (5'b00001), .out(shifter_1_out));
  Negator #(.width(16)) negator_1 (.in(ALU_alu_out), .out(negator_1_out));
  ALU_16_bit ALU_2 (
    .ALU_A_IN({{6{1'b0}}, Expo_in}), .ALU_B_IN(negator_1_out), .OP_CODE(3'b000),
    .ALU_OUT({ALU_2_alu_out[15], ALU_2_alu_out_2, ALU_2_alu_out[10], Expo_out}), .Z(ALU_2_z));  // open: N
  Shifter #(.width(32)) shifter_2 (.in(Significand), .\dist (ALU_alu_out[4:0]), .out(shifter_2_out));
  ALU_16_bit ALU_3 (
    .ALU_A_IN({ALU_2_alu_out[15], ALU_2_alu_out_2, ALU_2_alu_out[10], Expo_out}), .ALU_B_IN(16'h1),
    .OP_CODE(3'b000), .ALU_OUT(ALU_3_alu_out));  // open: Z, N
  _7432 u_7432_1 (
    ._1__1A(ALU_2_alu_out[15]), ._2__1B(ALU_2_z), ._3__1Y(n7432_1__3__1y));  // open: _4__2A, _5__2B, _6__2Y, _7__GND, _14__Vcc, _13__4B, _12__4A, _11__4Y, _10__3B, _9__3A, _8__3Y
  _74157 u_74157_1 (
    ._1__S(comparator_2_eq), ._2__A1(n7432_1__3__1y), ._3__B1(n7486_1__6__2y), ._4__Y1(Underflow),
    ._15__G(1'b0));  // open: _5__A2, _6__B2, _7__Y2, _8__GND, _16__Vcc, _14__A4, _13__B4, _12__Y4, _11__A3, _10__B3, _9__Y3
  MUX32bit MUX (._0(shifter_2_out), ._1(shifter_1_out), .Select(ALU_n), .out(signi_out));
  _7486 u_7486_1 (
    ._1__1A(ALU_3_alu_out[10]), ._2__1B(ALU_3_alu_out[15]), ._3__1Y(Overflow), ._4__2A(comparator_1_eq),
    ._5__2B(1'b1), ._6__2Y(n7486_1__6__2y));  // open: _7__GND, _14__Vcc, _13__4B, _12__4A, _11__4Y, _10__3B, _9__3A, _8__3Y
endmodule

module MUX32bit (
  input  [31:0] _0,
  input  [31:0] _1,
  input  Select,
  output [31:0] out
);

  wire [9:8] MUX_2_out;

  MUX24bit MUX (.X(_0[23:0]), .Y(_1[23:0]), .S(Select), .out_4(out[23:0]));
  MUX10bit MUX_2 (._0({2'b00, _0[31:24]}), ._1({2'b00, _1[31:24]}), .SELECT(Select), .OUT({MUX_2_out, out[31:24]}));
endmodule

module Round_Up_or_Not (
  input  [31:0] Input,
  output [31:0] toBeAdded
);

  wire n7432_1__3__1y, n7432_1__6__2y, n7432_1__8__3y, n7432_1__11__4y, n7432_2__3__1y, n7432_2__8__3y,
       n7432_2__11__4y;

  _7432 u_7432_1 (
    ._1__1A(Input[0]), ._2__1B(Input[1]), ._3__1Y(n7432_1__3__1y), ._4__2A(n7432_1__3__1y),
    ._5__2B(Input[2]), ._6__2Y(n7432_1__6__2y), ._13__4B(Input[5]), ._12__4A(n7432_1__8__3y),
    ._11__4Y(n7432_1__11__4y), ._10__3B(Input[3]), ._9__3A(n7432_1__6__2y), ._8__3Y(n7432_1__8__3y));  // open: _7__GND, _14__Vcc
  _7432 u_7432_2 (
    ._1__1A(n7432_1__11__4y), ._2__1B(Input[4]), ._3__1Y(n7432_2__3__1y), ._13__4B(n7432_2__3__1y),
    ._12__4A(Input[6]), ._11__4Y(n7432_2__11__4y), ._10__3B(n7432_2__11__4y), ._9__3A(Input[8]),
    ._8__3Y(n7432_2__8__3y));  // open: _4__2A, _5__2B, _6__2Y, _7__GND, _14__Vcc
  _7408 u_7408_1 (
    ._1__1A(n7432_2__8__3y), ._2__1B(Input[7]), ._3__1Y(toBeAdded[8]));  // open: _4__2A, _5__2B, _6__2Y, _7__GND, _14__Vcc, _13__4B, _12__4A, _11__4Y, _10__3B, _9__3A, _8__3Y

  assign {toBeAdded[31:9], toBeAdded[7:0]} = {31{1'b0}};

  // Notes on the sheet:
  //   G(L+R+S)
endmodule
