// Logisim project B2_Group01.circ as structural Verilog: 5 circuits, main circuit main
module main (
  input  in_1,
  output [15:0] out_2,
  output [7:0] PC,
  output [3:0] zero,
  output [3:0] t0,
  output [3:0] t1,
  output [3:0] t2,
  output [3:0] t3,
  output [3:0] t4,
  output [3:0] sp
);

  wire and_1_out, Clock_out, controlwithrom_1_alusrc, controlwithrom_1_bne, controlwithrom_1_branch,
       controlwithrom_1_jump, controlwithrom_1_memread, controlwithrom_1_memtoreg, controlwithrom_1_memwrite,
       controlwithrom_1_regdst, controlwithrom_1_regwrite, controlwithrom_1_shiftcontrol,
       controlwithrom_1_shiftleftorright, n74181_1_p10, or_1_out, xor_1_out;
  wire [3:0] multiplexer_1_out, multiplexer_2_out, multiplexer_5_out, multiplexer_6_out, multiplexer_7_out,
       multiplexer_8_out, n74181_1_p7, ram_1_data, register_file_v2_1_read01, register_file_v2_1_read02,
       shifter_1_out, shifter_2_out;
  wire [5:0] controlwithrom_1_alu_op;
  wire [7:0] adder_1_out, adder_2_out, bit_extender_1_out, multiplexer_3_out, multiplexer_4_out;

  Register To_Store_PC (.D(multiplexer_4_out), .Q(PC), .clk(Clock_out), .clr(in_1));  // open: en
  Adder adder_1 (.a(8'h1), .b(PC), .out(adder_1_out));  // open: cin, cout
  assign bit_extender_1_out = {{4{out_2[3]}}, out_2[3:0]};  // Bit_Extender bit_extender_1
  ROM #(.dataWidth(16)) rom_1 (.addr(PC), .data(out_2));  // open: sel
  Multiplexer #(.width(4), .enable("false")) multiplexer_1 (
    .in0(out_2[7:4]), .in1(out_2[3:0]), .out(multiplexer_1_out), .sel(controlwithrom_1_regdst));
  Clock Clock (.out(Clock_out));
  Adder adder_2 (.a(adder_1_out), .b(bit_extender_1_out), .out(adder_2_out));  // open: cin, cout
  controlWithRom controlwithrom_1 (
    .Opcode(out_2[15:12]), .Alu_Op(controlwithrom_1_alu_op), .RegDst(controlwithrom_1_regdst),
    .Jump(controlwithrom_1_jump), .Branch(controlwithrom_1_branch), .BNE(controlwithrom_1_bne),
    .MemRead(controlwithrom_1_memread), .MemtoReg(controlwithrom_1_memtoreg),
    .MemWrite(controlwithrom_1_memwrite), .AluSrc(controlwithrom_1_alusrc),
    .RegWrite(controlwithrom_1_regwrite), .ShiftControl(controlwithrom_1_shiftcontrol),
    .ShiftLeftOrRight(controlwithrom_1_shiftleftorright));
  register_file_v2 register_file_v2_1 (
    .ReadRegister01(out_2[11:8]), .ReadRegister02(out_2[7:4]), .WriteRegister(multiplexer_1_out),
    .Clk(Clock_out), .RegWrite(controlwithrom_1_regwrite), .DataToBeWritten(multiplexer_7_out),
    .Read01(register_file_v2_1_read01), .Read02(register_file_v2_1_read02), .zero(zero), .t0(t0), .t1(t1),
    .t2(t2), .t3(t3), .t4(t4), .sp(sp));  // open: sw_1_lw_0
  Multiplexer #(.width(4), .enable("false")) multiplexer_2 (
    .in0(register_file_v2_1_read02), .in1(out_2[3:0]), .out(multiplexer_2_out), .sel(controlwithrom_1_alusrc));
  // _74181 74181_1: pin names not known; wires that end beside it: controlwithrom_1_alu_op[3], controlwithrom_1_alu_op[2], controlwithrom_1_alu_op[1], controlwithrom_1_alu_op[0], controlwithrom_1_alu_op[4], controlwithrom_1_alu_op[5], n74181_1_p7, register_file_v2_1_read01, multiplexer_2_out, n74181_1_p10
  and and_1 (and_1_out, controlwithrom_1_branch, xor_1_out);
  xor xor_1 (xor_1_out, controlwithrom_1_bne, n74181_1_p10);
  Multiplexer #(.width(8), .enable("false")) multiplexer_3 (
    .in0(adder_1_out), .in1(adder_2_out), .out(multiplexer_3_out), .sel(and_1_out));
  RAM #(.addrWidth(4), .dataWidth(4), .bus("separate")) ram_1 (
    .addr(n74181_1_p7), .din(register_file_v2_1_read02), .data(ram_1_data), .str(controlwithrom_1_memwrite),
    .clk(Clock_out), .ld(controlwithrom_1_memread));  // open: sel, clr
  Shifter #(.width(4)) shifter_1 (.in(register_file_v2_1_read01), .\dist (out_2[1:0]), .out(shifter_1_out));
  Shifter #(.width(4), .shift("lr")) shifter_2 (
    .in(register_file_v2_1_read01), .\dist (out_2[1:0]), .out(shifter_2_out));
  or or_1 (or_1_out, out_2[2], out_2[3]);
  Multiplexer #(.width(8), .enable("false")) multiplexer_4 (
    .in0(multiplexer_3_out), .in1(out_2[11:4]), .out(multiplexer_4_out), .sel(controlwithrom_1_jump));
  Multiplexer #(.width(4), .enable("false")) multiplexer_5 (
    .in0(n74181_1_p7), .in1(ram_1_data), .out(multiplexer_5_out), .sel(controlwithrom_1_memtoreg));
  Multiplexer #(.width(4), .enable("false")) multiplexer_6 (
    .in0(shifter_1_out), .in1(shifter_2_out), .out(multiplexer_6_out), .sel(controlwithrom_1_shiftleftorright));
  Multiplexer #(.width(4), .enable("false")) multiplexer_7 (
    .in0(multiplexer_5_out), .in1(multiplexer_8_out), .out(multiplexer_7_out),
    .sel(controlwithrom_1_shiftcontrol));
  Multiplexer #(.width(4), .enable("false")) multiplexer_8 (
    .in0(multiplexer_6_out), .in1(4'b0000), .out(multiplexer_8_out), .sel(or_1_out));

  // Notes on the sheet:
  //   contents of rom_1 (hex, n*v repeats v):
  //   5023 203e 8231 d234 b135 6323 f331 3341 4190 e441 334 506f 6620 663f 4180 7131 f552 c531 e551 a225
  //   63f c324 630 4190 1128
endmodule

module control (
  input  [3:0] Opcode,
  output RegDst,
  output Jump,
  output Branch,
  output BranchNotEqual,
  output MemRead,
  output MemToReg,
  output [5:0] ALUOP,
  output MemWrite,
  output ALUSrc,
  output RegWrite,
  output ShiftControl,
  output ShiftLeftOrRight
);

  wire and_1_out, and_2_out, and_3_out, and_4_out, and_5_out, and_6_out, and_7_out, and_8_out, and_9_out,
       and_10_out, and_11_out, and_12_out, and_13_out, and_14_out, and_15_out, and_16_out, and_17_out,
       and_18_out, and_19_out, and_20_out, and_21_out, and_22_out, and_23_out, and_24_out, and_25_out,
       and_26_out, and_27_out, and_30_out, and_31_out, and_32_out, and_34_out, and_35_out, and_36_out,
       and_37_out, and_38_out, and_39_out, not_1_out, not_2_out, not_3_out, not_4_out, not_5_out, not_6_out,
       not_7_out, not_8_out, not_9_out, not_10_out, not_11_out, not_12_out, not_13_out, not_14_out,
       not_15_out, not_16_out, not_17_out, not_18_out, not_19_out, not_20_out, not_21_out, not_22_out,
       not_23_out, not_24_out, not_25_out, not_26_out, not_27_out, not_28_out, not_29_out, not_30_out,
       not_31_out, not_32_out, not_33_out, not_34_out, not_35_out, not_36_out, not_37_out, not_38_out,
       not_39_out, not_41_out, not_42_out, not_43_out, not_44_out, not_45_out, not_46_out, not_47_out,
       not_48_out, not_49_out, not_50_out, not_51_out, not_52_out, not_53_out, not_54_out, not_55_out;

  not not_1 (not_1_out, Opcode[1]);
  not not_2 (not_2_out, Opcode[0]);
  not not_3 (not_3_out, Opcode[3]);
  not not_4 (not_4_out, Opcode[2]);
  not not_5 (not_5_out, Opcode[1]);
  not not_6 (not_6_out, Opcode[0]);
  not not_7 (not_7_out, Opcode[3]);
  not not_8 (not_8_out, Opcode[2]);
  not not_9 (not_9_out, Opcode[2]);
  not not_10 (not_10_out, Opcode[0]);
  not not_11 (not_11_out, Opcode[3]);
  not not_12 (not_12_out, Opcode[2]);
  not not_13 (not_13_out, Opcode[1]);
  not not_14 (not_14_out, Opcode[3]);
  not not_15 (not_15_out, Opcode[2]);
  not not_16 (not_16_out, Opcode[2]);
  not not_17 (not_17_out, Opcode[0]);
  not not_18 (not_18_out, Opcode[3]);
  not not_19 (not_19_out, Opcode[1]);
  not not_20 (not_20_out, Opcode[0]);
  not not_21 (not_21_out, Opcode[3]);
  not not_22 (not_22_out, Opcode[1]);
  not not_23 (not_23_out, Opcode[0]);
  not not_24 (not_24_out, Opcode[2]);
  not not_25 (not_25_out, Opcode[1]);
  not not_26 (not_26_out, Opcode[0]);
  not not_27 (not_27_out, Opcode[3]);
  not not_28 (not_28_out, Opcode[2]);
  not not_29 (not_29_out, Opcode[0]);
  and and_1 (and_1_out, not_1_out, not_2_out);
  and and_2 (and_2_out, not_3_out, Opcode[2]);
  and and_3 (and_3_out, Opcode[3], not_4_out, not_5_out);
  and and_4 (and_4_out, Opcode[3], not_6_out);
  and and_5 (and_5_out, not_7_out, not_8_out, Opcode[0]);
  and and_6 (and_6_out, not_9_out, Opcode[1], not_10_out);
  and and_7 (and_7_out, not_11_out, Opcode[1], Opcode[0]);
  and and_8 (and_8_out, Opcode[3], Opcode[2], Opcode[0]);
  and and_9 (and_9_out, not_12_out, not_13_out, Opcode[0]);
  and and_10 (and_10_out, not_14_out, not_15_out, Opcode[1]);
  and and_11 (and_11_out, not_16_out, Opcode[1], not_17_out);
  and and_12 (and_12_out, not_18_out, Opcode[1], Opcode[0]);
  and and_13 (and_13_out, Opcode[3], Opcode[2]);
  and and_14 (and_14_out, not_19_out, not_20_out);
  and and_15 (and_15_out, not_21_out, Opcode[2], not_22_out);
  and and_16 (and_16_out, Opcode[2], not_23_out);
  and and_17 (and_17_out, Opcode[3], not_24_out, Opcode[0]);
  and and_18 (and_18_out, not_25_out, not_26_out);
  or or_1 (ALUOP[4], and_18_out, and_19_out);
  and and_19 (and_19_out, not_27_out, Opcode[2]);
  and and_20 (and_20_out, Opcode[2], Opcode[1], Opcode[0]);
  and and_21 (and_21_out, Opcode[3], not_28_out, Opcode[0]);
  and and_22 (and_22_out, Opcode[3], Opcode[1]);
  and and_23 (and_23_out, Opcode[3], Opcode[2], not_29_out);
  or or_2 (ALUOP[0], and_1_out, and_2_out, and_3_out, and_4_out);
  or or_3 (ALUOP[1], and_5_out, and_6_out, and_7_out, and_8_out);
  or or_4 (ALUOP[2], and_9_out, and_10_out, and_11_out, and_12_out, and_13_out);
  or or_5 (ALUOP[3], and_14_out, and_15_out, and_16_out, and_17_out);
  or or_6 (ALUOP[5], and_20_out, and_21_out, and_22_out, and_23_out);
  not not_30 (not_30_out, Opcode[3]);
  not not_31 (not_31_out, Opcode[2]);
  not not_32 (not_32_out, Opcode[1]);
  not not_33 (not_33_out, Opcode[2]);
  not not_34 (not_34_out, Opcode[1]);
  not not_35 (not_35_out, Opcode[3]);
  not not_36 (not_36_out, Opcode[1]);
  not not_37 (not_37_out, Opcode[0]);
  not not_38 (not_38_out, Opcode[3]);
  not not_39 (not_39_out, Opcode[2]);
  not not_40 (BranchNotEqual, Opcode[1]);
  not not_41 (not_41_out, Opcode[2]);
  not not_42 (not_42_out, Opcode[0]);
  not not_43 (not_43_out, Opcode[3]);
  not not_44 (not_44_out, Opcode[1]);
  not not_45 (not_45_out, Opcode[0]);
  not not_46 (not_46_out, Opcode[3]);
  not not_47 (not_47_out, Opcode[0]);
  not not_48 (not_48_out, Opcode[3]);
  not not_49 (not_49_out, Opcode[0]);
  not not_50 (not_50_out, Opcode[0]);
  not not_51 (not_51_out, Opcode[3]);
  not not_52 (not_52_out, Opcode[1]);
  not not_53 (not_53_out, Opcode[0]);
  not not_54 (not_54_out, Opcode[2]);
  not not_55 (not_55_out, Opcode[0]);
  and and_24 (and_24_out, not_30_out, Opcode[2], Opcode[1]);
  and and_25 (and_25_out, Opcode[3], not_31_out, not_32_out);
  and and_26 (and_26_out, Opcode[3], not_33_out, Opcode[0]);
  and and_27 (and_27_out, Opcode[3], not_34_out, Opcode[0]);
  and and_28 (Jump, not_35_out, Opcode[2], not_36_out, not_37_out);
  and and_29 (Branch, not_38_out, not_39_out, Opcode[0]);
  and and_30 (and_30_out, not_41_out, not_42_out);
  and and_31 (and_31_out, not_43_out, not_44_out);
  and and_32 (and_32_out, Opcode[2], Opcode[1], not_45_out);
  and and_33 (MemWrite, not_46_out, Opcode[2], Opcode[1], not_47_out);
  and and_34 (and_34_out, not_48_out, not_49_out);
  and and_35 (and_35_out, Opcode[1], not_50_out);
  and and_36 (and_36_out, not_51_out, Opcode[2], not_52_out);
  and and_37 (and_37_out, Opcode[2], not_53_out);
  and and_38 (and_38_out, not_54_out, not_55_out);
  and and_39 (and_39_out, Opcode[2], Opcode[0]);
  and and_40 (ShiftControl, Opcode[3], Opcode[2], Opcode[1]);
  or or_7 (RegDst, and_24_out, and_25_out, and_26_out, and_27_out);
  or or_8 (MemRead, and_30_out, Opcode[3]);
  or or_9 (MemToReg, and_31_out, and_32_out);
  or or_10 (ALUSrc, and_34_out, and_35_out, and_36_out, and_37_out);
  or or_11 (RegWrite, and_38_out, and_39_out, Opcode[3]);

  assign ShiftLeftOrRight = Opcode[0];

  // Notes on the sheet:
  //   W
  //   X
  //   Y
  //   Z
  //   C
  //   M
endmodule

module register_file (
  input  [2:0] ReadRegister01,
  input  [2:0] ReadRegister01_2,
  input  [2:0] WriteRegister,
  input  CLK,
  input  RegWrite,
  input  [3:0] DataToBeWritten
);

  wire [2:0] multiplexer_1_out, multiplexer_2_out;

  Multiplexer #(.width(3), .enable("false")) multiplexer_1 (
    .in0(ReadRegister01), .in1(WriteRegister), .out(multiplexer_1_out), .sel(RegWrite));
  Multiplexer #(.width(3), .enable("false")) multiplexer_2 (
    .in0(ReadRegister01_2), .in1(WriteRegister), .out(multiplexer_2_out), .sel(RegWrite));
  // NOT_Gate not_1 is placed but not wired
  RAM #(.addrWidth(3), .dataWidth(4), .bus("asynch")) ram_1 (.addr(multiplexer_1_out));  // open: data, sel, ld, clr
  RAM #(.addrWidth(3), .dataWidth(4), .bus("separate")) ram_2 (
    .addr(multiplexer_2_out), .din(DataToBeWritten));  // open: data, str, sel, clk, ld, clr
endmodule

module register_file_v2 (
  input  [3:0] ReadRegister01,
  input  [3:0] ReadRegister02,
  input  [3:0] WriteRegister,
  input  Clk,
  input  RegWrite,
  input  [3:0] DataToBeWritten,
  input  sw_1_lw_0,
  output [3:0] Read01,
  output [3:0] Read02,
  output [3:0] zero,
  output [3:0] t0,
  output [3:0] t1,
  output [3:0] t2,
  output [3:0] t3,
  output [3:0] t4,
  output [3:0] sp
);

  wire and_1_out, decoder_1_out1, decoder_1_out2, decoder_1_out3, decoder_1_out4, decoder_1_out5,
       decoder_1_out6, not_1_out;
  wire [3:0] adder_1_out, adder_2_out, multiplexer_1_out, multiplexer_2_out;

  not not_1 (not_1_out, ReadRegister01[0]);
  Decoder #(.select(3), .disabled(0)) decoder_1 (
    .out1(decoder_1_out1), .out2(decoder_1_out2), .out3(decoder_1_out3), .out4(decoder_1_out4),
    .out5(decoder_1_out5), .out6(decoder_1_out6), .sel(WriteRegister[2:0]), .en(RegWrite));  // open: out0, out7
  and and_1 (and_1_out, not_1_out, ReadRegister01[1], ReadRegister01[2]);
  Register #(.width(4)) u_t0 (.D(DataToBeWritten), .en(decoder_1_out1), .Q(t0), .clk(Clk));  // open: clr
  Register #(.width(4)) u_t1 (.D(DataToBeWritten), .en(decoder_1_out2), .Q(t1), .clk(Clk));  // open: clr
  Register #(.width(4)) u_t2 (.D(DataToBeWritten), .en(decoder_1_out3), .Q(t2), .clk(Clk));  // open: clr
  Register #(.width(4)) u_t3 (.D(DataToBeWritten), .en(decoder_1_out4), .Q(t3), .clk(Clk));  // open: clr
  Register #(.width(4)) u_t4 (.D(DataToBeWritten), .en(decoder_1_out5), .Q(t4), .clk(Clk));  // open: clr
  Register #(.width(4), .trigger("falling")) u_sp (
    .D(multiplexer_2_out), .en(and_1_out), .Q(sp), .clk(Clk));  // open: clr
  Adder #(.width(4)) adder_1 (.a(sp), .b(4'b1111), .out(adder_1_out));  // open: cin, cout
  Multiplexer #(.width(4), .disabled(0), .enable("false")) multiplexer_1 (
    .in0(sp), .in1(adder_1_out), .out(multiplexer_1_out), .sel(sw_1_lw_0));
  Adder #(.width(4)) adder_2 (.a(sp), .b(4'b0001), .out(adder_2_out));  // open: cin, cout
  Multiplexer #(.width(4), .disabled(0), .enable("false")) multiplexer_2 (
    .in0(adder_2_out), .in1(adder_1_out), .out(multiplexer_2_out), .sel(sw_1_lw_0));
  Multiplexer #(.select(3), .width(4), .disabled(0), .enable("false")) multiplexer_3 (
    .in0(4'b0000), .in1(t0), .in2(t1), .in3(t2), .in4(t3), .in5(t4), .in6(multiplexer_1_out), .out(Read01),
    .sel(ReadRegister01[2:0]));  // open: in7
  Multiplexer #(.select(3), .width(4), .disabled(0), .enable("false")) multiplexer_4 (
    .in0(4'b0000), .in1(t0), .in2(t1), .in3(t2), .in4(t3), .in5(t4), .in6(multiplexer_1_out), .out(Read02),
    .sel(ReadRegister02[2:0]));  // open: in7

  assign zero = 4'b0000;
endmodule

module controlWithRom (
  input  [3:0] Opcode,
  output [5:0] Alu_Op,
  output RegDst,
  output Jump,
  output Branch,
  output BNE,
  output MemRead,
  output MemtoReg,
  output MemWrite,
  output AluSrc,
  output RegWrite,
  output ShiftControl,
  output ShiftLeftOrRight
);

  ROM #(.addrWidth(4), .dataWidth(17)) rom_1 (
    .addr(Opcode),
    .data({ShiftLeftOrRight, ShiftControl, RegWrite, AluSrc, MemWrite, MemtoReg, MemRead, BNE, Branch, Jump, RegDst, Alu_Op}));  // open: sel

  // Notes on the sheet:
  //   contents of rom_1 (hex, n*v repeats v):
  //   6c19 306 6006 106 80 6019 3019 406e 4059 406b 602e 4061 602b 4046 c000 1c000
endmodule
