// Logisim project control.circ as structural Verilog: 2 circuits, main circuit main
module main (
  input  a,
  input  b,
  input  c,
  input  d,
  output w,
  output x,
  output y,
  output z,
  output c_2,
  output m
);

  wire and_1_out, and_2_out, and_3_out, and_4_out, and_5_out, and_6_out, and_7_out, and_8_out, and_9_out,
       and_10_out, and_11_out, and_12_out, and_13_out, and_14_out, and_15_out, and_16_out, and_17_out,
       and_18_out, and_19_out, and_20_out, and_21_out, and_22_out, and_23_out, not_1_out, not_2_out,
       not_3_out, not_4_out, not_5_out, not_6_out, not_7_out, not_8_out, not_9_out, not_10_out, not_11_out,
       not_12_out, not_13_out, not_14_out, not_15_out, not_16_out, not_17_out, not_18_out, not_19_out,
       not_20_out, not_21_out, not_22_out, not_23_out, not_24_out, not_25_out, not_26_out, not_27_out,
       not_28_out, not_29_out;

  not not_1 (not_1_out, c);
  and and_1 (and_1_out, not_1_out, not_2_out);
  not not_2 (not_2_out, d);
  not not_3 (not_3_out, a);
  and and_2 (and_2_out, not_3_out, b);
  and and_3 (and_3_out, a, not_4_out, not_5_out);
  not not_4 (not_4_out, b);
  not not_5 (not_5_out, c);
  and and_4 (and_4_out, a, not_6_out);
  not not_6 (not_6_out, d);
  not not_7 (not_7_out, a);
  and and_5 (and_5_out, not_7_out, not_8_out, d);
  not not_8 (not_8_out, b);
  not not_9 (not_9_out, b);
  and and_6 (and_6_out, not_9_out, c, not_10_out);
  not not_10 (not_10_out, d);
  not not_11 (not_11_out, a);
  and and_7 (and_7_out, not_11_out, c, d);
  and and_8 (and_8_out, a, b, d);
  not not_12 (not_12_out, b);
  not not_13 (not_13_out, c);
  and and_9 (and_9_out, not_12_out, not_13_out, d);
  not not_14 (not_14_out, a);
  not not_15 (not_15_out, b);
  and and_10 (and_10_out, not_14_out, not_15_out, c);
  not not_16 (not_16_out, b);
  and and_11 (and_11_out, not_16_out, c, not_17_out);
  not not_17 (not_17_out, d);
  not not_18 (not_18_out, a);
  and and_12 (and_12_out, not_18_out, c, d);
  and and_13 (and_13_out, a, b);
  not not_19 (not_19_out, c);
  and and_14 (and_14_out, not_19_out, not_20_out);
  not not_20 (not_20_out, d);
  not not_21 (not_21_out, a);
  and and_15 (and_15_out, not_21_out, b, not_22_out);
  not not_22 (not_22_out, c);
  and and_16 (and_16_out, b, not_23_out);
  not not_23 (not_23_out, d);
  and and_17 (and_17_out, a, not_24_out, d);
  not not_24 (not_24_out, b);
  not not_25 (not_25_out, c);
  and and_18 (and_18_out, not_25_out, not_26_out);
  not not_26 (not_26_out, d);
  not not_27 (not_27_out, a);
  and and_19 (and_19_out, not_27_out, b);
  and and_20 (and_20_out, b, c, d);
  not not_28 (not_28_out, b);
  and and_21 (and_21_out, a, not_28_out, d);
  and and_22 (and_22_out, a, c);
  and and_23 (and_23_out, a, b, not_29_out);
  not not_29 (not_29_out, d);
  or or_1 (w, and_1_out, and_2_out, and_3_out, and_4_out);
  or or_2 (x, and_5_out, and_6_out, and_7_out, and_8_out);
  or or_3 (y, and_9_out, and_10_out, and_11_out, and_12_out, and_13_out);
  or or_4 (z, and_14_out, and_15_out, and_16_out, and_17_out);
  or or_5 (c_2, and_18_out, and_19_out);
  or or_6 (m, and_20_out, and_21_out, and_22_out, and_23_out);
endmodule

module control2 (
  input  [3:0] Opcode,
  output RegDst,
  output Jump,
  output Branch,
  output BranchNotEqual,
  output MemRead,
  output MemToReg,
  output [5:0] ALUOP,
  output MemWrite,
  output ALUSrc,
  output RegWrite,
  output ShiftControl,
  output ShiftLeftOrRight
);

  wire and_1_out, and_2_out, and_3_out, and_4_out, and_5_out, and_6_out, and_7_out, and_8_out, and_9_out,
       and_10_out, and_11_out, and_12_out, and_13_out, and_14_out, and_15_out, and_16_out, and_17_out,
       and_18_out, and_19_out, and_20_out, and_21_out, and_22_out, and_23_out, and_24_out, and_25_out,
       and_26_out, and_27_out, and_30_out, and_31_out, and_32_out, and_34_out, and_35_out, and_36_out,
       and_37_out, and_38_out, and_39_out, not_1_out, not_2_out, not_3_out, not_4_out, not_5_out, not_6_out,
       not_7_out, not_8_out, not_9_out, not_10_out, not_11_out, not_12_out, not_13_out, not_14_out,
       not_15_out, not_16_out, not_17_out, not_18_out, not_19_out, not_20_out, not_21_out, not_22_out,
       not_23_out, not_24_out, not_25_out, not_26_out, not_27_out, not_28_out, not_29_out, not_30_out,
       not_31_out, not_32_out, not_33_out, not_34_out, not_35_out, not_36_out, not_37_out, not_38_out,
       not_39_out, not_41_out, not_42_out, not_43_out, not_44_out, not_45_out, not_46_out, not_47_out,
       not_48_out, not_49_out, not_50_out, not_51_out, not_52_out, not_53_out, not_54_out, not_55_out;

  not not_1 (not_1_out, Opcode[1]);
  not not_2 (not_2_out, Opcode[0]);
  not not_3 (not_3_out, Opcode[3]);
  not not_4 (not_4_out, Opcode[2]);
  not not_5 (not_5_out, Opcode[1]);
  not not_6 (not_6_out, Opcode[0]);
  not not_7 (not_7_out, Opcode[3]);
  not not_8 (not_8_out, Opcode[2]);
  not not_9 (not_9_out, Opcode[2]);
  not not_10 (not_10_out, Opcode[0]);
  not not_11 (not_11_out, Opcode[3]);
  not not_12 (not_12_out, Opcode[2]);
  not not_13 (not_13_out, Opcode[1]);
  not not_14 (not_14_out, Opcode[3]);
  not not_15 (not_15_out, Opcode[2]);
  not not_16 (not_16_out, Opcode[2]);
  not not_17 (not_17_out, Opcode[0]);
  not not_18 (not_18_out, Opcode[3]);
  not not_19 (not_19_out, Opcode[1]);
  not not_20 (not_20_out, Opcode[0]);
  not not_21 (not_21_out, Opcode[3]);
  not not_22 (not_22_out, Opcode[1]);
  not not_23 (not_23_out, Opcode[0]);
  not not_24 (not_24_out, Opcode[2]);
  not not_25 (not_25_out, Opcode[1]);
  not not_26 (not_26_out, Opcode[0]);
  not not_27 (not_27_out, Opcode[3]);
  not not_28 (not_28_out, Opcode[2]);
  not not_29 (not_29_out, Opcode[0]);
  and and_1 (and_1_out, not_1_out, not_2_out);
  and and_2 (and_2_out, not_3_out, Opcode[2]);
  and and_3 (and_3_out, Opcode[3], not_4_out, not_5_out);
  and and_4 (and_4_out, Opcode[3], not_6_out);
  and and_5 (and_5_out, not_7_out, not_8_out, Opcode[0]);
  and and_6 (and_6_out, not_9_out, Opcode[1], not_10_out);
  and and_7 (and_7_out, not_11_out, Opcode[1], Opcode[0]);
  and and_8 (and_8_out, Opcode[3], Opcode[2], Opcode[0]);
  and and_9 (and_9_out, not_12_out, not_13_out, Opcode[0]);
  and and_10 (and_10_out, not_14_out, not_15_out, Opcode[1]);
  and and_11 (and_11_out, not_16_out, Opcode[1], not_17_out);
  and and_12 (and_12_out, not_18_out, Opcode[1], Opcode[0]);
  and and_13 (and_13_out, Opcode[3], Opcode[2]);
  and and_14 (and_14_out, not_19_out, not_20_out);
  and and_15 (and_15_out, not_21_out, Opcode[2], not_22_out);
  and and_16 (and_16_out, Opcode[2], not_23_out);
  and and_17 (and_17_out, Opcode[3], not_24_out, Opcode[0]);
  and and_18 (and_18_out, not_25_out, not_26_out);
  or or_1 (ALUOP[4], and_18_out, and_19_out);
  and and_19 (and_19_out, not_27_out, Opcode[2]);
  and and_20 (and_20_out, Opcode[2], Opcode[1], Opcode[0]);
  and and_21 (and_21_out, Opcode[3], not_28_out, Opcode[0]);
  and and_22 (and_22_out, Opcode[3], Opcode[1]);
  and and_23 (and_23_out, Opcode[3], Opcode[2], not_29_out);
  or or_2 (ALUOP[0], and_1_out, and_2_out, and_3_out, and_4_out);
  or or_3 (ALUOP[1], and_5_out, and_6_out, and_7_out, and_8_out);
  or or_4 (ALUOP[2], and_9_out, and_10_out, and_11_out, and_12_out, and_13_out);
  or or_5 (ALUOP[3], and_14_out, and_15_out, and_16_out, and_17_out);
  or or_6 (ALUOP[5], and_20_out, and_21_out, and_22_out, and_23_out);
  not not_30 (not_30_out, Opcode[3]);
  not not_31 (not_31_out, Opcode[2]);
  not not_32 (not_32_out, Opcode[1]);
  not not_33 (not_33_out, Opcode[2]);
  not not_34 (not_34_out, Opcode[1]);
  not not_35 (not_35_out, Opcode[3]);
  not not_36 (not_36_out, Opcode[1]);
  not not_37 (not_37_out, Opcode[0]);
  not not_38 (not_38_out, Opcode[3]);
  not not_39 (not_39_out, Opcode[2]);
  not not_40 (BranchNotEqual, Opcode[1]);
  not not_41 (not_41_out, Opcode[2]);
  not not_42 (not_42_out, Opcode[0]);
  not not_43 (not_43_out, Opcode[3]);
  not not_44 (not_44_out, Opcode[1]);
  not not_45 (not_45_out, Opcode[0]);
  not not_46 (not_46_out, Opcode[3]);
  not not_47 (not_47_out, Opcode[0]);
  not not_48 (not_48_out, Opcode[3]);
  not not_49 (not_49_out, Opcode[0]);
  not not_50 (not_50_out, Opcode[0]);
  not not_51 (not_51_out, Opcode[3]);
  not not_52 (not_52_out, Opcode[1]);
  not not_53 (not_53_out, Opcode[0]);
  not not_54 (not_54_out, Opcode[2]);
  not not_55 (not_55_out, Opcode[0]);
  and and_24 (and_24_out, not_30_out, Opcode[2], Opcode[1]);
  and and_25 (and_25_out, Opcode[3], not_31_out, not_32_out);
  and and_26 (and_26_out, Opcode[3], not_33_out, Opcode[0]);
  and and_27 (and_27_out, Opcode[3], not_34_out, Opcode[0]);
  and and_28 (Jump, not_35_out, Opcode[2], not_36_out, not_37_out);
  and and_29 (Branch, not_38_out, not_39_out, Opcode[0]);
  and and_30 (and_30_out, not_41_out, not_42_out);
  and and_31 (and_31_out, not_43_out, not_44_out);
  and and_32 (and_32_out, Opcode[2], Opcode[1], not_45_out);
  and and_33 (MemWrite, not_46_out, Opcode[2], Opcode[1], not_47_out);
  and and_34 (and_34_out, not_48_out, not_49_out);
  and and_35 (and_35_out, Opcode[1], not_50_out);
  and and_36 (and_36_out, not_51_out, Opcode[2], not_52_out);
  and and_37 (and_37_out, Opcode[2], not_53_out);
  and and_38 (and_38_out, not_54_out, not_55_out);
  and and_39 (and_39_out, Opcode[2], Opcode[0]);
  and and_40 (ShiftControl, Opcode[3], Opcode[2], Opcode[1]);
  or or_7 (RegDst, and_24_out, and_25_out, and_26_out, and_27_out);
  or or_8 (MemRead, and_30_out, Opcode[3]);
  or or_9 (MemToReg, and_31_out, and_32_out);
  or or_10 (ALUSrc, and_34_out, and_35_out, and_36_out, and_37_out);
  or or_11 (RegWrite, and_38_out, and_39_out, Opcode[3]);

  assign ShiftLeftOrRight = Opcode[0];

  // Notes on the sheet:
  //   W
  //   X
  //   Y
  //   Z
  //   C
  //   M
endmodule
